// Logisim project 2 Display_16_4.circ as structural Verilog: 2 circuits, main circuit main
module main (
  input  in_1,
  input  in_2,
  input  in_3,
  input  in_4,
  input  in_5,
  input  in_6,
  input  in_7,
  input  in_8,
  input  in_9,
  input  in_10,
  input  in_11,
  input  in_12,
  input  in_13,
  input  in_14,
  input  in_15,
  input  in_16
);

  wire A_out, B_out, C_out, D_out, dp_out, E_out, encoder_1_y0, encoder_1_y1, encoder_1_y2, encoder_1_y3,
       F0_out, F1_out, F2_out, F3_out, F4_out, F5_out, F6_out, F7_out, F8_out, F9_out, F10_out, F11_out,
       F12_out, F13_out, F14_out, F15_out, F_out, G_out, not_1_out, not_2_out, not_3_out, not_4_out;

  encoder encoder_1 (
    .A0(in_1), .A1(in_2), .A2(in_3), .A3(in_4), .A4(in_5), .A5(in_6), .A6(in_7), .A7(in_8), .A8(in_9),
    .A9(in_10), .A10(in_11), .A11(in_12), .A12(in_13), .A13(in_14), .A14(in_15), .A15(in_16),
    .Y0(encoder_1_y0), .Y1(encoder_1_y1), .Y2(encoder_1_y2), .Y3(encoder_1_y3));
  not not_1 (not_1_out, encoder_1_y0);
  not not_2 (not_2_out, encoder_1_y1);
  not not_3 (not_3_out, encoder_1_y2);
  not not_4 (not_4_out, encoder_1_y3);
  and F0 (F0_out, not_1_out, not_2_out, not_3_out, not_4_out);
  and F1 (F1_out, encoder_1_y0, not_4_out, not_3_out, not_2_out);
  and F2 (F2_out, encoder_1_y1, not_1_out, not_3_out, not_4_out);
  and F3 (F3_out, encoder_1_y0, encoder_1_y1, not_3_out, not_4_out);
  and F4 (F4_out, not_4_out, encoder_1_y2, not_2_out, not_1_out);
  and F5 (F5_out, not_4_out, encoder_1_y2, not_2_out, encoder_1_y0);
  and F6 (F6_out, not_1_out, encoder_1_y1, encoder_1_y2, not_4_out);
  and F7 (F7_out, encoder_1_y0, encoder_1_y1, encoder_1_y2, not_4_out);
  and F8 (F8_out, not_1_out, not_2_out, not_3_out, encoder_1_y3);
  and F9 (F9_out, encoder_1_y0, not_2_out, not_3_out, encoder_1_y3);
  and F10 (F10_out, encoder_1_y1, not_3_out, not_1_out, encoder_1_y3);
  and F11 (F11_out, encoder_1_y1, not_3_out, encoder_1_y0, encoder_1_y3);
  and F12 (F12_out, not_2_out, not_1_out, encoder_1_y2, encoder_1_y3);
  and F13 (F13_out, not_2_out, encoder_1_y0, encoder_1_y2, encoder_1_y3);
  and F14 (F14_out, encoder_1_y1, not_1_out, encoder_1_y2, encoder_1_y3);
  and F15 (F15_out, encoder_1_y1, encoder_1_y0, encoder_1_y2, encoder_1_y3);
  or G (G_out, F2_out, F3_out, F4_out, F5_out, F6_out, F8_out, F9_out, F10_out, F11_out, F14_out, F15_out, F13_out);
  or F (F_out, F0_out, F4_out, F5_out, F6_out, F8_out, F9_out, F10_out, F11_out, F12_out, F14_out, F15_out);
  or A (A_out, F0_out, F2_out, F3_out, F5_out, F6_out, F7_out, F8_out, F9_out, F10_out, F12_out, F14_out, F15_out);
  or B (B_out, F0_out, F1_out, F2_out, F3_out, F4_out, F7_out, F8_out, F9_out, F10_out, F13_out);
  // OR_Gate dp has open pins: out=dp_out
  _7_Segment_Display u_7_segment_display_1 (
    .g(G_out), .f(F_out), .a(A_out), .b(B_out), .e(E_out), .d(D_out), .c(C_out), .dp(dp_out));
  or C (C_out, F0_out, F1_out, F3_out, F4_out, F5_out, F6_out, F7_out, F8_out, F9_out, F10_out, F11_out, F13_out);
  or D (D_out, F0_out, F2_out, F3_out, F5_out, F6_out, F8_out, F9_out, F11_out, F12_out, F13_out, F14_out);
  or E (E_out, F0_out, F2_out, F6_out, F8_out, F10_out, F11_out, F12_out, F13_out, F14_out, F15_out);
endmodule

module encoder (
  input  A0,
  input  A1,
  input  A2,
  input  A3,
  input  A4,
  input  A5,
  input  A6,
  input  A7,
  input  A8,
  input  A9,
  input  A10,
  input  A11,
  input  A12,
  input  A13,
  input  A14,
  input  A15,
  output Y0,
  output Y1,
  output Y2,
  output Y3
);

  wire and_1_out, not_1_out;

  not not_1 (not_1_out, A0);
  and and_1 (and_1_out, not_1_out, A0);
  or or_1 (Y0, A1, A3, A5, A7, and_1_out, A9, A11, A13, A15);
  or or_2 (Y1, A2, A3, A6, A7, A10, A11, A14, A15);
  or or_3 (Y2, A4, A5, A6, A7, A12, A13, A14, A15);
  or or_4 (Y3, A8, A9, A10, A11, A12, A13, A14, A15);
endmodule
