// Logisim project 24_38.circ as structural Verilog: 2 circuits, main circuit main
module main (
  input  C,
  input  B,
  input  A,
  output Y0,
  output Y1,
  output Y2,
  output Y3,
  output Y4,
  output Y5,
  output Y6,
  output Y7
);

  wire ls139_1_out_3, ls139_1_out_4, ls139_1_out_5, ls139_1_out_6, not_1_out;

  LS139 ls139_1 (
    .A(B), .B(A), .out_3(ls139_1_out_3), .out_4(ls139_1_out_4), .out_5(ls139_1_out_5), .out_6(ls139_1_out_6));
  not not_1 (not_1_out, C);
  and and_1 (Y0, ls139_1_out_3, not_1_out);
  and and_2 (Y1, ls139_1_out_4, not_1_out);
  and and_3 (Y2, ls139_1_out_5, not_1_out);
  and and_4 (Y3, ls139_1_out_6, not_1_out);
  and and_5 (Y4, ls139_1_out_3, C);
  and and_6 (Y5, ls139_1_out_4, C);
  and and_7 (Y6, ls139_1_out_5, C);
  and and_8 (Y7, ls139_1_out_6, C);

  // Notes on the sheet:
  //   C输入端口当做使能
  //   第一次未考虑4567情况下Y0-Y3输出，导致Y0,Y4同时为1，遂添加非门与门保证Y0-Y3不影响Y4-Y7输出
endmodule

module LS139 (
  input  A,
  input  B,
  output out_3,
  output out_4,
  output out_5,
  output out_6
);

  wire not_1_out, not_2_out;

  not not_1 (not_1_out, A);
  not not_2 (not_2_out, B);
  and and_1 (out_3, not_1_out, not_2_out);
  and and_2 (out_4, not_1_out, B);
  and and_3 (out_5, A, not_2_out);
  and and_4 (out_6, A, B);
endmodule
