// Logisim project 2_to_4.circ as structural Verilog: 1 circuit, main circuit main
module main (
  input  A,
  input  B,
  output Y1,
  output Y2,
  output Y4,
  output Y3
);

  wire not_1_out, not_2_out;

  not not_1 (not_1_out, A);
  not not_2 (not_2_out, B);
  and and_1 (Y1, A, B);
  and and_2 (Y2, A, not_2_out);
  and and_3 (Y4, not_1_out, not_2_out);
  and and_4 (Y3, not_1_out, B);
endmodule
