// Logisim project 16_4_encoder.circ as structural Verilog: 1 circuit, main circuit main
module main (
);

  wire and_2_out, and_3_out, and_4_out, and_5_out, and_6_out, and_7_out, and_8_out, and_9_out, and_10_out,
       and_11_out, and_12_out, and_13_out, and_14_out, and_15_out, and_16_out, and_17_out, and_18_out,
       and_19_out, and_20_out, and_21_out, and_22_out, and_23_out, and_24_out, and_25_out, and_26_out,
       and_27_out, and_28_out, and_29_out, and_30_out, and_31_out, and_32_out, dipswitch_1_sw1,
       dipswitch_1_sw2, dipswitch_1_sw3, dipswitch_1_sw4, dipswitch_1_sw5, dipswitch_1_sw6, dipswitch_1_sw7,
       dipswitch_1_sw8, dipswitch_1_sw9, dipswitch_1_sw10, dipswitch_1_sw11, dipswitch_1_sw12,
       dipswitch_1_sw13, dipswitch_1_sw14, dipswitch_1_sw15, dipswitch_1_sw16, not_1_out, not_2_out,
       not_3_out, not_4_out, not_5_out, not_6_out, not_7_out, not_8_out, not_9_out, not_10_out, not_11_out,
       not_12_out, not_13_out, not_14_out, not_15_out, not_16_out, not_17_out, not_18_out, not_19_out,
       not_20_out, or_1_out, or_2_out, or_3_out, or_4_out, or_5_out, or_6_out, or_7_out, or_8_out, or_9_out,
       or_10_out, or_11_out;

  not not_1 (not_1_out, dipswitch_1_sw1);
  not not_2 (not_2_out, dipswitch_1_sw2);
  not not_3 (not_3_out, dipswitch_1_sw3);
  not not_4 (not_4_out, dipswitch_1_sw4);
  not not_5 (not_5_out, dipswitch_1_sw5);
  not not_6 (not_6_out, dipswitch_1_sw6);
  not not_7 (not_7_out, dipswitch_1_sw7);
  DipSwitch #(.number(16)) dipswitch_1 (
    .sw1(dipswitch_1_sw1), .sw2(dipswitch_1_sw2), .sw3(dipswitch_1_sw3), .sw4(dipswitch_1_sw4),
    .sw5(dipswitch_1_sw5), .sw6(dipswitch_1_sw6), .sw7(dipswitch_1_sw7), .sw8(dipswitch_1_sw8),
    .sw9(dipswitch_1_sw9), .sw10(dipswitch_1_sw10), .sw11(dipswitch_1_sw11), .sw12(dipswitch_1_sw12),
    .sw13(dipswitch_1_sw13), .sw14(dipswitch_1_sw14), .sw15(dipswitch_1_sw15), .sw16(dipswitch_1_sw16));
  not not_8 (not_8_out, dipswitch_1_sw8);
  not not_9 (not_9_out, dipswitch_1_sw9);
  not not_10 (not_10_out, dipswitch_1_sw10);
  not not_11 (not_11_out, dipswitch_1_sw11);
  not not_12 (not_12_out, dipswitch_1_sw12);
  not not_13 (not_13_out, dipswitch_1_sw13);
  not not_14 (not_14_out, dipswitch_1_sw14);
  not not_15 (not_15_out, dipswitch_1_sw15);
  not not_16 (not_16_out, dipswitch_1_sw16);
  // AND_Gate and_1 has open pins: in0=dipswitch_1_sw1, in1=not_2_out, in2=not_3_out, in3=not_4_out, in4=not_5_out, in5=not_6_out, in6=not_7_out, in7=not_8_out, in8=not_9_out, in9=not_10_out, in10=not_11_out, in11=not_12_out, in12=not_13_out, in13=not_14_out, in14=not_15_out, in15=not_16_out, out=open
  and and_2 (and_2_out, dipswitch_1_sw2, not_1_out, not_3_out, not_4_out, not_5_out, not_6_out, not_7_out, not_8_out, not_9_out, not_10_out, not_11_out, not_12_out, not_13_out, not_14_out, not_15_out, not_16_out);
  and and_3 (and_3_out, dipswitch_1_sw3, not_1_out, not_2_out, not_4_out, not_5_out, not_6_out, not_7_out, not_8_out, not_9_out, not_10_out, not_11_out, not_12_out, not_13_out, not_14_out, not_15_out, not_16_out);
  and and_4 (and_4_out, dipswitch_1_sw4, not_1_out, not_2_out, not_3_out, not_5_out, not_6_out, not_7_out, not_8_out, not_9_out, not_10_out, not_11_out, not_12_out, not_13_out, not_14_out, not_15_out, not_16_out);
  and and_5 (and_5_out, dipswitch_1_sw5, not_1_out, not_2_out, not_3_out, not_4_out, not_6_out, not_7_out, not_8_out, not_9_out, not_10_out, not_11_out, not_12_out, not_13_out, not_14_out, not_15_out, not_16_out);
  and and_6 (and_6_out, dipswitch_1_sw6, not_1_out, not_2_out, not_3_out, not_5_out, not_4_out, not_7_out, not_8_out, not_9_out, not_10_out, not_11_out, not_12_out, not_13_out, not_14_out, not_15_out, not_16_out);
  and and_7 (and_7_out, dipswitch_1_sw7, not_1_out, not_2_out, not_3_out, not_5_out, not_6_out, not_4_out, not_8_out, not_9_out, not_10_out, not_11_out, not_12_out, not_13_out, not_14_out, not_15_out, not_16_out);
  and and_8 (and_8_out, dipswitch_1_sw8, not_1_out, not_2_out, not_4_out, not_5_out, not_6_out, not_7_out, not_3_out, not_9_out, not_10_out, not_11_out, not_12_out, not_13_out, not_14_out, not_15_out, not_16_out);
  and and_9 (and_9_out, dipswitch_1_sw9, not_1_out, not_2_out, not_4_out, not_5_out, not_6_out, not_7_out, not_8_out, not_3_out, not_10_out, not_11_out, not_12_out, not_13_out, not_14_out, not_15_out, not_16_out);
  and and_10 (and_10_out, dipswitch_1_sw10, not_1_out, not_2_out, not_3_out, not_5_out, not_6_out, not_7_out, not_8_out, not_9_out, not_4_out, not_11_out, not_12_out, not_13_out, not_14_out, not_15_out, not_16_out);
  and and_11 (and_11_out, dipswitch_1_sw11, not_1_out, not_2_out, not_3_out, not_5_out, not_6_out, not_7_out, not_8_out, not_9_out, not_10_out, not_4_out, not_12_out, not_13_out, not_14_out, not_15_out, not_16_out);
  and and_12 (and_12_out, dipswitch_1_sw12, not_1_out, not_2_out, not_3_out, not_5_out, not_6_out, not_7_out, not_8_out, not_9_out, not_10_out, not_11_out, not_4_out, not_13_out, not_14_out, not_15_out, not_16_out);
  and and_13 (and_13_out, dipswitch_1_sw13, not_1_out, not_2_out, not_3_out, not_5_out, not_6_out, not_7_out, not_8_out, not_9_out, not_10_out, not_11_out, not_12_out, not_4_out, not_14_out, not_15_out, not_16_out);
  and and_14 (and_14_out, dipswitch_1_sw14, not_1_out, not_2_out, not_3_out, not_5_out, not_6_out, not_7_out, not_8_out, not_9_out, not_10_out, not_11_out, not_12_out, not_13_out, not_4_out, not_15_out, not_16_out);
  and and_15 (and_15_out, dipswitch_1_sw15, not_1_out, not_2_out, not_3_out, not_5_out, not_6_out, not_7_out, not_8_out, not_9_out, not_10_out, not_11_out, not_12_out, not_13_out, not_14_out, not_4_out, not_16_out);
  and and_16 (and_16_out, dipswitch_1_sw16, not_1_out, not_2_out, not_3_out, not_5_out, not_6_out, not_7_out, not_8_out, not_9_out, not_10_out, not_11_out, not_12_out, not_13_out, not_14_out, not_15_out, not_4_out);
  or or_1 (or_1_out, and_16_out, and_15_out, and_14_out, and_13_out, and_12_out, and_11_out, and_10_out, and_9_out);
  or or_2 (or_2_out, and_16_out, and_15_out, and_14_out, and_13_out, and_8_out, and_7_out, and_6_out, and_5_out);
  or or_3 (or_3_out, and_16_out, and_15_out, and_12_out, and_11_out, and_8_out, and_7_out, and_4_out, and_3_out);
  or or_4 (or_4_out, and_16_out, and_14_out, and_12_out, and_10_out, and_8_out, and_6_out, and_4_out, and_2_out);
  not not_17 (not_17_out, or_4_out);
  not not_18 (not_18_out, or_3_out);
  not not_19 (not_19_out, or_2_out);
  not not_20 (not_20_out, or_1_out);
  and and_17 (and_17_out, not_17_out, not_18_out, not_19_out, not_20_out);
  and and_18 (and_18_out, or_4_out, not_18_out, not_19_out, not_20_out);
  and and_19 (and_19_out, or_3_out, not_17_out, not_19_out, not_20_out);
  and and_20 (and_20_out, or_4_out, or_3_out, not_19_out, not_20_out);
  and and_21 (and_21_out, or_2_out, not_17_out, not_18_out, not_20_out);
  and and_22 (and_22_out, or_2_out, or_4_out, not_18_out, not_20_out);
  and and_23 (and_23_out, or_2_out, or_3_out, not_17_out, not_20_out);
  and and_24 (and_24_out, or_4_out, or_3_out, or_2_out, not_20_out);
  and and_25 (and_25_out, or_1_out, not_17_out, not_18_out, not_19_out);
  and and_26 (and_26_out, or_1_out, or_4_out, not_19_out, not_18_out);
  and and_27 (and_27_out, or_1_out, not_19_out, or_3_out, not_17_out);
  and and_28 (and_28_out, or_1_out, not_19_out, or_3_out, or_4_out);
  and and_29 (and_29_out, or_1_out, or_2_out, not_18_out, not_17_out);
  and and_30 (and_30_out, or_1_out, or_2_out, not_18_out, or_4_out);
  and and_31 (and_31_out, or_1_out, or_2_out, or_3_out, not_17_out);
  and and_32 (and_32_out, or_1_out, or_2_out, or_3_out, or_4_out);
  or or_5 (or_5_out, and_29_out, and_17_out, and_19_out, and_20_out, and_22_out, and_23_out, and_25_out, and_26_out, and_31_out, and_30_out, and_28_out);
  or or_6 (or_6_out, and_27_out, and_17_out, and_19_out, and_23_out, and_25_out, and_32_out, and_31_out, and_30_out, and_29_out, and_28_out);
  or or_7 (or_7_out, and_27_out, and_19_out, and_20_out, and_21_out, and_22_out, and_23_out, and_25_out, and_26_out, and_32_out, and_31_out, and_30_out, and_28_out);
  _7_Segment_Display u_7_segment_display_1 (
    .g(or_7_out), .f(or_8_out), .a(or_9_out), .b(or_10_out), .e(or_6_out), .d(or_5_out), .c(or_11_out));  // open: dp
  or or_8 (or_8_out, and_27_out, and_17_out, and_21_out, and_22_out, and_23_out, and_25_out, and_26_out, and_32_out, and_31_out, and_29_out, and_28_out);
  or or_9 (or_9_out, and_27_out, and_17_out, and_19_out, and_20_out, and_22_out, and_23_out, and_24_out, and_25_out, and_26_out, and_32_out, and_31_out, and_29_out);
  or or_10 (or_10_out, and_17_out, and_18_out, and_19_out, and_20_out, and_21_out, and_24_out, and_25_out, and_26_out, and_30_out, and_27_out);
  or or_11 (or_11_out, and_27_out, and_22_out, and_17_out, and_18_out, and_20_out, and_21_out, and_23_out, and_24_out, and_25_out, and_28_out, and_30_out, and_26_out);
endmodule
