// Logisim project 16_4_pri_encoder.circ as structural Verilog: 2 circuits, main circuit main
module main (
  input  A0,
  input  A1,
  input  A2,
  input  A3,
  input  A4,
  input  A5,
  input  A6,
  input  A7,
  input  A8,
  input  A9,
  input  A10,
  input  A11,
  input  A12,
  input  A13,
  input  A14,
  input  A15,
  output Y0,
  output Y1,
  output Y2,
  output Y3
);

  wire encoder_4_to_2_1_v, encoder_4_to_2_1_y0, encoder_4_to_2_1_y1, encoder_4_to_2_2_v, encoder_4_to_2_2_y0,
       encoder_4_to_2_2_y1, encoder_4_to_2_3_v, encoder_4_to_2_3_y0, encoder_4_to_2_3_y1, encoder_4_to_2_4_v,
       encoder_4_to_2_4_y0, encoder_4_to_2_4_y1;

  encoder_4_to_2 encoder_4_to_2_1 (
    .A0(A0), .A1(A1), .A2(A2), .A3(A3), .Y0(encoder_4_to_2_1_y0), .Y1(encoder_4_to_2_1_y1),
    .V(encoder_4_to_2_1_v));
  encoder_4_to_2 encoder_4_to_2_2 (
    .A0(A4), .A1(A5), .A2(A6), .A3(A7), .Y0(encoder_4_to_2_2_y0), .Y1(encoder_4_to_2_2_y1),
    .V(encoder_4_to_2_2_v));
  encoder_4_to_2 encoder_4_to_2_3 (
    .A0(A8), .A1(A9), .A2(A10), .A3(A11), .Y0(encoder_4_to_2_3_y0), .Y1(encoder_4_to_2_3_y1),
    .V(encoder_4_to_2_3_v));
  encoder_4_to_2 encoder_4_to_2_4 (
    .A0(A12), .A1(A13), .A2(A14), .A3(A15), .Y0(encoder_4_to_2_4_y0), .Y1(encoder_4_to_2_4_y1),
    .V(encoder_4_to_2_4_v));
  or or_1 (Y0, encoder_4_to_2_1_y0, encoder_4_to_2_2_y0, encoder_4_to_2_3_y0, encoder_4_to_2_4_y0);
  or or_2 (Y1, encoder_4_to_2_1_y1, encoder_4_to_2_2_y1, encoder_4_to_2_3_y1, encoder_4_to_2_4_y1);
  encoder_4_to_2 encoder_4_to_2_5 (
    .A0(encoder_4_to_2_1_v), .A1(encoder_4_to_2_2_v), .A2(encoder_4_to_2_3_v), .A3(encoder_4_to_2_4_v),
    .Y0(Y2), .Y1(Y3));  // open: V
endmodule

module encoder_4_to_2 (
  input  A0,
  input  A1,
  input  A2,
  input  A3,
  output Y0,
  output Y1,
  output V
);

  wire and_1_out, not_1_out;

  not not_1 (not_1_out, A2);
  and and_1 (and_1_out, A1, not_1_out);
  or or_1 (V, A0, A1, A2, A3);
  or or_2 (Y0, and_1_out, A3);
  or or_3 (Y1, A2, A3);
endmodule
