// Logisim project 2to4_decoder_1.circ as structural Verilog: 2 circuits, main circuit main
module main (
);

  encoder2to4 encoder2to4_1 ();  // open: A, B, Y0, Y1, Y2, Y3
endmodule

module encoder2to4 (
  input  A,
  input  B,
  output Y0,
  output Y1,
  output Y2,
  output Y3
);

  wire not_1_out, not_2_out;

  not not_1 (not_1_out, A);
  not not_2 (not_2_out, B);
  and and_1 (Y0, not_1_out, not_2_out);
  and and_2 (Y1, A, not_2_out);
  and and_3 (Y2, not_1_out, B);
  and and_4 (Y3, A, B);
endmodule
