// Logisim project 3to8_decoder.circ as structural Verilog: 2 circuits, main circuit main
module main (
  input  EN,
  input  A,
  input  B,
  input  C,
  output Y0,
  output Y1,
  output Y2,
  output Y3,
  output Y4,
  output Y5,
  output Y6,
  output Y7
);

  wire and_1_out, and_2_out, and_3_out, not_1_out;

  and and_1 (and_1_out, EN, A);
  and and_2 (and_2_out, EN, B);
  and and_3 (and_3_out, EN, C);
  not not_1 (not_1_out, and_3_out);
  encoder2to4 encoder2to4_1 (.EN(not_1_out), .A(and_1_out), .B(and_2_out), .Y0(Y0), .Y1(Y1), .Y2(Y2), .Y3(Y3));
  encoder2to4 encoder2to4_2 (.EN(and_3_out), .A(and_1_out), .B(and_2_out), .Y0(Y4), .Y1(Y5), .Y2(Y6), .Y3(Y7));
endmodule

module encoder2to4 (
  input  EN,
  input  A,
  input  B,
  output Y0,
  output Y1,
  output Y2,
  output Y3
);

  wire not_1_out, not_2_out;

  not not_1 (not_1_out, A);
  not not_2 (not_2_out, B);
  and and_1 (Y0, not_1_out, EN, not_2_out);
  and and_2 (Y1, A, EN, not_2_out);
  and and_3 (Y2, not_1_out, EN, B);
  and and_4 (Y3, A, EN, B);
endmodule
