// Logisim project 7Seg_Decoder_2.circ as structural Verilog: 1 circuit, main circuit main
module main (
);

  wire and_1_out, and_2_out, and_3_out, and_4_out, and_5_out, and_6_out, and_7_out, and_8_out, and_9_out,
       and_10_out, and_11_out, and_12_out, and_13_out, and_14_out, and_15_out, and_16_out, and_17_out,
       dipswitch_1_p1, dipswitch_1_p2, dipswitch_1_p3, dipswitch_1_p4, dipswitch_1_p5, nor_1_out, not_1_out,
       not_2_out, not_3_out, not_4_out, not_5_out, or_1_out, or_2_out, or_3_out, or_4_out, or_5_out,
       or_6_out, or_7_out;

  // DipSwitch #(.number(5)) dipswitch_1: pin names not known; wires that end beside it: dipswitch_1_p1, dipswitch_1_p2, dipswitch_1_p3, dipswitch_1_p4, dipswitch_1_p5
  not not_1 (not_1_out, dipswitch_1_p1);
  not not_2 (not_2_out, dipswitch_1_p2);
  not not_3 (not_3_out, dipswitch_1_p3);
  not not_4 (not_4_out, dipswitch_1_p4);
  and and_1 (and_1_out, not_1_out, not_2_out, not_3_out, not_4_out);
  and and_2 (and_2_out, dipswitch_1_p1, not_2_out, not_3_out, not_4_out);
  and and_3 (and_3_out, dipswitch_1_p2, not_1_out, not_3_out, not_4_out);
  and and_4 (and_4_out, dipswitch_1_p1, dipswitch_1_p2, not_3_out, not_4_out);
  and and_5 (and_5_out, dipswitch_1_p3, not_1_out, not_2_out, not_4_out);
  and and_6 (and_6_out, dipswitch_1_p3, dipswitch_1_p1, not_2_out, not_4_out);
  and and_7 (and_7_out, dipswitch_1_p3, dipswitch_1_p2, not_1_out, not_4_out);
  and and_8 (and_8_out, dipswitch_1_p1, dipswitch_1_p2, dipswitch_1_p3, not_4_out);
  and and_9 (and_9_out, dipswitch_1_p4, not_1_out, not_2_out, not_3_out);
  and and_10 (and_10_out, dipswitch_1_p4, dipswitch_1_p1, not_3_out, not_2_out);
  and and_11 (and_11_out, dipswitch_1_p4, not_3_out, dipswitch_1_p5, dipswitch_1_p2, not_1_out);
  and and_12 (and_12_out, dipswitch_1_p4, not_3_out, dipswitch_1_p5, dipswitch_1_p2, dipswitch_1_p1);
  and and_13 (and_13_out, dipswitch_1_p4, dipswitch_1_p3, dipswitch_1_p5, not_2_out, not_1_out);
  and and_14 (and_14_out, dipswitch_1_p4, dipswitch_1_p3, dipswitch_1_p5, not_2_out, dipswitch_1_p1);
  and and_15 (and_15_out, dipswitch_1_p4, dipswitch_1_p3, dipswitch_1_p5, dipswitch_1_p2, not_1_out);
  and and_16 (and_16_out, dipswitch_1_p4, dipswitch_1_p3, dipswitch_1_p5, dipswitch_1_p2, dipswitch_1_p1);
  not not_5 (not_5_out, dipswitch_1_p5);
  or or_1 (or_1_out, and_13_out, and_1_out, and_3_out, and_4_out, and_6_out, and_7_out, and_9_out, and_10_out, and_15_out, and_14_out, and_12_out);
  or or_2 (or_2_out, and_11_out, and_1_out, and_3_out, and_7_out, and_9_out, and_16_out, and_15_out, and_14_out, and_13_out, and_12_out);
  or or_3 (or_3_out, and_11_out, and_3_out, and_4_out, and_5_out, and_6_out, and_7_out, and_9_out, and_10_out, and_16_out, and_15_out, and_14_out, and_12_out);
  or or_4 (or_4_out, and_11_out, and_1_out, and_5_out, and_6_out, and_7_out, and_9_out, and_10_out, and_16_out, and_15_out, and_13_out, and_12_out);
  _7_Segment_Display u_7_segment_display_1 (
    .g(or_3_out), .f(or_4_out), .a(or_5_out), .b(or_6_out), .e(or_2_out), .d(or_1_out), .c(or_7_out),
    .dp(and_17_out));
  or or_5 (or_5_out, and_11_out, and_1_out, and_3_out, and_4_out, and_6_out, and_7_out, and_8_out, and_9_out, and_10_out, and_16_out, and_15_out, and_13_out);
  or or_6 (or_6_out, and_1_out, and_2_out, and_3_out, and_4_out, and_5_out, and_8_out, and_9_out, and_10_out, and_14_out, and_11_out);
  nor nor_1 (nor_1_out, and_1_out, and_2_out, and_3_out, and_4_out, and_5_out, and_6_out, and_7_out, and_8_out, and_9_out, and_10_out);
  and and_17 (and_17_out, not_5_out, nor_1_out);
  or or_7 (or_7_out, and_11_out, and_6_out, and_1_out, and_2_out, and_4_out, and_5_out, and_7_out, and_8_out, and_9_out, and_12_out, and_14_out, and_10_out);
endmodule
