// Logisim project Seg_16_4_pri_encoder.circ as structural Verilog: 3 circuits, main circuit main
module main (
);

  wire decoder4_16_1_y0, decoder4_16_1_y1, decoder4_16_1_y2, decoder4_16_1_y3, decoder4_16_1_y4,
       decoder4_16_1_y5, decoder4_16_1_y6, decoder4_16_1_y7, decoder4_16_1_y8, decoder4_16_1_y9,
       decoder4_16_1_ya, decoder4_16_1_yb, decoder4_16_1_yc, decoder4_16_1_yd, decoder4_16_1_ye,
       decoder4_16_1_yf, dipswitch_1_p1, dipswitch_1_p2, dipswitch_1_p3, dipswitch_1_p4, dipswitch_1_p5,
       dipswitch_1_p6, dipswitch_1_p7, dipswitch_1_p8, dipswitch_1_p9, dipswitch_1_p10, dipswitch_1_p11,
       dipswitch_1_p12, dipswitch_1_p13, dipswitch_1_p14, dipswitch_1_p15, dipswitch_1_p16,
       encoder_4_to_2_1_v, encoder_4_to_2_1_y0, encoder_4_to_2_1_y1, encoder_4_to_2_2_v, encoder_4_to_2_2_y0,
       encoder_4_to_2_2_y1, encoder_4_to_2_3_v, encoder_4_to_2_3_y0, encoder_4_to_2_3_y1, encoder_4_to_2_4_v,
       encoder_4_to_2_4_y0, encoder_4_to_2_4_y1, encoder_4_to_2_5_y0, encoder_4_to_2_5_y1, or_1_out,
       or_2_out, or_3_out, or_4_out, or_5_out, or_6_out, or_7_out, or_8_out, or_9_out;

  // DipSwitch #(.number(16)) dipswitch_1: pin names not known; wires that end beside it: dipswitch_1_p1, dipswitch_1_p2, dipswitch_1_p3, dipswitch_1_p4, dipswitch_1_p5, dipswitch_1_p6, dipswitch_1_p7, dipswitch_1_p8, dipswitch_1_p9, dipswitch_1_p10, dipswitch_1_p11, dipswitch_1_p12, dipswitch_1_p13, dipswitch_1_p14, dipswitch_1_p15, dipswitch_1_p16
  encoder_4_to_2 encoder_4_to_2_1 (
    .A0(dipswitch_1_p1), .A1(dipswitch_1_p2), .A2(dipswitch_1_p3), .A3(dipswitch_1_p4),
    .Y0(encoder_4_to_2_1_y0), .Y1(encoder_4_to_2_1_y1), .V(encoder_4_to_2_1_v));
  encoder_4_to_2 encoder_4_to_2_2 (
    .A0(dipswitch_1_p5), .A1(dipswitch_1_p6), .A2(dipswitch_1_p7), .A3(dipswitch_1_p8),
    .Y0(encoder_4_to_2_2_y0), .Y1(encoder_4_to_2_2_y1), .V(encoder_4_to_2_2_v));
  encoder_4_to_2 encoder_4_to_2_3 (
    .A0(dipswitch_1_p9), .A1(dipswitch_1_p10), .A2(dipswitch_1_p11), .A3(dipswitch_1_p12),
    .Y0(encoder_4_to_2_3_y0), .Y1(encoder_4_to_2_3_y1), .V(encoder_4_to_2_3_v));
  encoder_4_to_2 encoder_4_to_2_4 (
    .A0(dipswitch_1_p13), .A1(dipswitch_1_p14), .A2(dipswitch_1_p15), .A3(dipswitch_1_p16),
    .Y0(encoder_4_to_2_4_y0), .Y1(encoder_4_to_2_4_y1), .V(encoder_4_to_2_4_v));
  or or_1 (or_1_out, encoder_4_to_2_1_y0, encoder_4_to_2_2_y0, encoder_4_to_2_3_y0, encoder_4_to_2_4_y0);
  or or_2 (or_2_out, encoder_4_to_2_1_y1, encoder_4_to_2_2_y1, encoder_4_to_2_3_y1, encoder_4_to_2_4_y1);
  encoder_4_to_2 encoder_4_to_2_5 (
    .A0(encoder_4_to_2_1_v), .A1(encoder_4_to_2_2_v), .A2(encoder_4_to_2_3_v), .A3(encoder_4_to_2_4_v),
    .Y0(encoder_4_to_2_5_y0), .Y1(encoder_4_to_2_5_y1));  // open: V
  decoder4_16 decoder4_16_1 (
    .A0(or_1_out), .A1(or_2_out), .A2(encoder_4_to_2_5_y0), .A3(encoder_4_to_2_5_y1), .Y0(decoder4_16_1_y0),
    .Y1(decoder4_16_1_y1), .Y2(decoder4_16_1_y2), .Y3(decoder4_16_1_y3), .Y4(decoder4_16_1_y4),
    .Y5(decoder4_16_1_y5), .Y6(decoder4_16_1_y6), .Y7(decoder4_16_1_y7), .Y8(decoder4_16_1_y8),
    .Y9(decoder4_16_1_y9), .YA(decoder4_16_1_ya), .Yb(decoder4_16_1_yb), .YC(decoder4_16_1_yc),
    .Yd(decoder4_16_1_yd), .YE(decoder4_16_1_ye), .YF(decoder4_16_1_yf));
  or or_3 (or_3_out, decoder4_16_1_y0, decoder4_16_1_y2, decoder4_16_1_y3, decoder4_16_1_y5, decoder4_16_1_y6, decoder4_16_1_y8, decoder4_16_1_y9, decoder4_16_1_yb, decoder4_16_1_yc, decoder4_16_1_yd, decoder4_16_1_ye);
  or or_4 (or_4_out, decoder4_16_1_y0, decoder4_16_1_y2, decoder4_16_1_y6, decoder4_16_1_y8, decoder4_16_1_ya, decoder4_16_1_yb, decoder4_16_1_yc, decoder4_16_1_yd, decoder4_16_1_ye, decoder4_16_1_yf);
  or or_5 (or_5_out, decoder4_16_1_y2, decoder4_16_1_y3, decoder4_16_1_y4, decoder4_16_1_y5, decoder4_16_1_y6, decoder4_16_1_y8, decoder4_16_1_y9, decoder4_16_1_ya, decoder4_16_1_yb, decoder4_16_1_yd, decoder4_16_1_ye, decoder4_16_1_yf);
  _7_Segment_Display u_7_segment_display_1 (
    .g(or_5_out), .f(or_6_out), .a(or_7_out), .b(or_8_out), .e(or_4_out), .d(or_3_out), .c(or_9_out));  // open: dp
  or or_6 (or_6_out, decoder4_16_1_y0, decoder4_16_1_y4, decoder4_16_1_y5, decoder4_16_1_y6, decoder4_16_1_y8, decoder4_16_1_y9, decoder4_16_1_ya, decoder4_16_1_yb, decoder4_16_1_yc, decoder4_16_1_ye, decoder4_16_1_yf);
  or or_7 (or_7_out, decoder4_16_1_y0, decoder4_16_1_y2, decoder4_16_1_y3, decoder4_16_1_y5, decoder4_16_1_y6, decoder4_16_1_y7, decoder4_16_1_y8, decoder4_16_1_y9, decoder4_16_1_ya, decoder4_16_1_yc, decoder4_16_1_ye, decoder4_16_1_yf);
  or or_8 (or_8_out, decoder4_16_1_y0, decoder4_16_1_y1, decoder4_16_1_y2, decoder4_16_1_y3, decoder4_16_1_y4, decoder4_16_1_y7, decoder4_16_1_y8, decoder4_16_1_y9, decoder4_16_1_ya, decoder4_16_1_yd);
  or or_9 (or_9_out, decoder4_16_1_y0, decoder4_16_1_y1, decoder4_16_1_y3, decoder4_16_1_y4, decoder4_16_1_y5, decoder4_16_1_y6, decoder4_16_1_y7, decoder4_16_1_y8, decoder4_16_1_y9, decoder4_16_1_ya, decoder4_16_1_yb, decoder4_16_1_yd);
endmodule

module encoder_4_to_2 (
  input  A0,
  input  A1,
  input  A2,
  input  A3,
  output Y0,
  output Y1,
  output V
);

  wire and_1_out, not_1_out;

  not not_1 (not_1_out, A2);
  and and_1 (and_1_out, A1, not_1_out);
  or or_1 (V, A0, A1, A2, A3);
  or or_2 (Y0, and_1_out, A3);
  or or_3 (Y1, A2, A3);
endmodule

module decoder4_16 (
  input  A0,
  input  A1,
  input  A2,
  input  A3,
  output Y0,
  output Y1,
  output Y2,
  output Y3,
  output Y4,
  output Y5,
  output Y6,
  output Y7,
  output Y8,
  output Y9,
  output YA,
  output Yb,
  output YC,
  output Yd,
  output YE,
  output YF
);

  wire not_1_out, not_2_out, not_3_out, not_4_out;

  not not_1 (not_1_out, A3);
  not not_2 (not_2_out, A2);
  not not_3 (not_3_out, A1);
  not not_4 (not_4_out, A0);
  and and_1 (Y0, not_4_out, not_3_out, not_2_out, not_1_out);
  and and_2 (Y1, not_3_out, A0, not_2_out, not_1_out);
  and and_3 (Y2, A1, not_2_out, not_1_out, not_4_out);
  and and_4 (Y3, A1, not_2_out, not_1_out, A0);
  and and_5 (Y4, not_3_out, A2, not_1_out, not_4_out);
  and and_6 (Y5, not_3_out, A2, not_1_out, A0);
  and and_7 (Y6, A1, A2, not_1_out, not_4_out);
  and and_8 (Y7, A1, A2, not_1_out, A0);
  and and_9 (Y8, not_3_out, not_2_out, A3, not_4_out);
  and and_10 (Y9, not_3_out, not_2_out, A3, A0);
  and and_11 (YA, A1, not_2_out, A3, not_4_out);
  and and_12 (Yb, A1, not_2_out, A3, A0);
  and and_13 (YC, not_3_out, A2, A3, not_4_out);
  and and_14 (Yd, not_3_out, A2, A3, A0);
  and and_15 (YE, A1, A2, A3, not_4_out);
  and and_16 (YF, A1, A2, A3, A0);
endmodule
