// Logisim project XNOR_1.circ as structural Verilog: 1 circuit, main circuit main
module main (
  input  A,
  input  B,
  output Y
);

  wire and_1_out, nor_1_out;

  and and_1 (and_1_out, A, B);
  nor nor_1 (nor_1_out, A, B);
  or or_1 (Y, and_1_out, nor_1_out);
endmodule
