// Logisim project adder4.circ as structural Verilog: 4 circuits, main circuit main
module main (
  input  b1,
  input  b2,
  input  b3,
  input  b0,
  input  a3,
  input  a2,
  input  a1,
  input  a0
);

  wire fulladder_1_cout, fulladder_1_s, fulladder_2_cout, fulladder_2_s, fulladder_3_cout, fulladder_3_s,
       halfadder_1_c, halfadder_1_s, segdecoder_1_a, segdecoder_1_b, segdecoder_1_c, segdecoder_1_d,
       segdecoder_1_e, segdecoder_1_f, segdecoder_1_g, segdecoder_2_a, segdecoder_2_b, segdecoder_2_c,
       segdecoder_2_d, segdecoder_2_e, segdecoder_2_f, segdecoder_2_g, segdecoder_3_a, segdecoder_3_b,
       segdecoder_3_c, segdecoder_3_d, segdecoder_3_e, segdecoder_3_f, segdecoder_3_g;

  halfadder halfadder_1 (.a(a0), .b(b0), .s(halfadder_1_s), .c(halfadder_1_c));
  fulladder fulladder_1 (.a(a1), .b(b1), .Cin(halfadder_1_c), .s(fulladder_1_s), .Cout(fulladder_1_cout));
  fulladder fulladder_2 (.a(a2), .b(b2), .Cin(fulladder_1_cout), .s(fulladder_2_s), .Cout(fulladder_2_cout));
  SegDecoder segdecoder_1 (
    .in_1(b0), .in_2(b1), .in_3(b2), .in_4(b3), .B(segdecoder_1_b), .A(segdecoder_1_a), .F(segdecoder_1_f),
    .G(segdecoder_1_g), .E(segdecoder_1_e), .D(segdecoder_1_d), .C(segdecoder_1_c));
  fulladder fulladder_3 (.a(a3), .b(b3), .Cin(fulladder_2_cout), .s(fulladder_3_s), .Cout(fulladder_3_cout));
  SegDecoder segdecoder_2 (
    .in_1(a0), .in_2(a1), .in_3(a2), .in_4(a3), .B(segdecoder_2_b), .A(segdecoder_2_a), .F(segdecoder_2_f),
    .G(segdecoder_2_g), .E(segdecoder_2_e), .D(segdecoder_2_d), .C(segdecoder_2_c));
  _7_Segment_Display u_7_segment_display_1 (
    .g(segdecoder_1_g), .f(segdecoder_1_f), .a(segdecoder_1_a), .b(segdecoder_1_b), .e(segdecoder_1_e),
    .d(segdecoder_1_d), .c(segdecoder_1_c));  // open: dp
  LED led_1 (.in(fulladder_3_cout));
  _7_Segment_Display a (
    .g(segdecoder_2_g), .f(segdecoder_2_f), .a(segdecoder_2_a), .b(segdecoder_2_b), .e(segdecoder_2_e),
    .d(segdecoder_2_d), .c(segdecoder_2_c));  // open: dp
  SegDecoder segdecoder_3 (
    .in_1(halfadder_1_s), .in_2(fulladder_1_s), .in_3(fulladder_2_s), .in_4(fulladder_3_s),
    .B(segdecoder_3_b), .A(segdecoder_3_a), .F(segdecoder_3_f), .G(segdecoder_3_g), .E(segdecoder_3_e),
    .D(segdecoder_3_d), .C(segdecoder_3_c));
  _7_Segment_Display u_7_segment_display_2 (
    .g(segdecoder_3_g), .f(segdecoder_3_f), .a(segdecoder_3_a), .b(segdecoder_3_b), .e(segdecoder_3_e),
    .d(segdecoder_3_d), .c(segdecoder_3_c));  // open: dp

  // Notes on the sheet:
  //   b
  //   a
  //   s
endmodule

module SegDecoder (
  input  in_1,
  input  in_2,
  input  in_3,
  input  in_4,
  output B,
  output A,
  output F,
  output G,
  output E,
  output D,
  output C
);

  wire and_1_out, and_2_out, and_3_out, and_4_out, and_5_out, and_6_out, and_7_out, and_8_out, and_9_out,
       and_10_out, and_11_out, and_12_out, and_13_out, and_14_out, and_15_out, and_16_out, not_1_out,
       not_2_out, not_3_out, not_4_out;

  not not_1 (not_1_out, in_1);
  not not_2 (not_2_out, in_2);
  not not_3 (not_3_out, in_3);
  not not_4 (not_4_out, in_4);
  and and_1 (and_1_out, not_1_out, not_2_out, not_3_out, not_4_out);
  and and_2 (and_2_out, in_1, not_2_out, not_3_out, not_4_out);
  and and_3 (and_3_out, in_2, not_1_out, not_3_out, not_4_out);
  and and_4 (and_4_out, in_1, in_2, not_3_out, not_4_out);
  and and_5 (and_5_out, in_3, not_1_out, not_2_out, not_4_out);
  and and_6 (and_6_out, in_3, in_1, not_2_out, not_4_out);
  and and_7 (and_7_out, in_3, in_2, not_1_out, not_4_out);
  and and_8 (and_8_out, in_1, in_2, in_3, not_4_out);
  and and_9 (and_9_out, in_4, not_1_out, not_2_out, not_3_out);
  and and_10 (and_10_out, in_4, in_1, not_3_out, not_2_out);
  and and_11 (and_11_out, in_4, not_3_out, in_2, not_1_out);
  and and_12 (and_12_out, in_4, not_3_out, in_2, in_1);
  and and_13 (and_13_out, in_4, in_3, not_2_out, not_1_out);
  and and_14 (and_14_out, in_4, in_3, not_2_out, in_1);
  and and_15 (and_15_out, in_4, in_3, in_2, not_1_out);
  and and_16 (and_16_out, in_4, in_3, in_2, in_1);
  or or_1 (D, and_13_out, and_1_out, and_3_out, and_4_out, and_6_out, and_7_out, and_9_out, and_10_out, and_15_out, and_14_out, and_12_out);
  or or_2 (E, and_11_out, and_1_out, and_3_out, and_7_out, and_9_out, and_16_out, and_15_out, and_14_out, and_13_out, and_12_out);
  or or_3 (G, and_11_out, and_3_out, and_4_out, and_5_out, and_6_out, and_7_out, and_9_out, and_10_out, and_16_out, and_15_out, and_14_out, and_12_out);
  or or_4 (F, and_11_out, and_1_out, and_5_out, and_6_out, and_7_out, and_9_out, and_10_out, and_16_out, and_15_out, and_13_out, and_12_out);
  or or_5 (A, and_11_out, and_1_out, and_3_out, and_4_out, and_6_out, and_7_out, and_8_out, and_9_out, and_10_out, and_16_out, and_15_out, and_13_out);
  or or_6 (B, and_1_out, and_2_out, and_3_out, and_4_out, and_5_out, and_8_out, and_9_out, and_10_out, and_14_out, and_11_out);
  or or_7 (C, and_11_out, and_6_out, and_1_out, and_2_out, and_4_out, and_5_out, and_7_out, and_8_out, and_9_out, and_12_out, and_14_out, and_10_out);
endmodule

module halfadder (
  input  a,
  input  b,
  output s,
  output c
);

  xor xor_1 (s, a, b);
  and and_1 (c, a, b);
endmodule

module fulladder (
  input  a,
  input  b,
  input  Cin,
  output s,
  output Cout
);

  wire and_1_out, and_2_out, xor_1_out;

  xor xor_1 (xor_1_out, a, b);
  and and_1 (and_1_out, a, b);
  xor xor_2 (s, xor_1_out, Cin);
  and and_2 (and_2_out, xor_1_out, Cin);
  or or_1 (Cout, and_1_out, and_2_out);
endmodule
