// Logisim project fulladder1.circ as structural Verilog: 2 circuits, main circuit main
module main (
  input  Cin,
  input  a,
  input  b,
  output S,
  output Cout
);

  wire halfadder_1_c, halfadder_1_s, halfadder_2_c;

  halfadder halfadder_1 (.a(a), .b(b), .s(halfadder_1_s), .c(halfadder_1_c));
  halfadder halfadder_2 (.a(Cin), .b(halfadder_1_s), .s(S), .c(halfadder_2_c));
  or or_1 (Cout, halfadder_1_c, halfadder_2_c);
endmodule

module halfadder (
  input  a,
  input  b,
  output s,
  output c
);

  xor xor_1 (s, a, b);
  and and_1 (c, a, b);
endmodule
