// Logisim project mux_4to1.circ as structural Verilog: 2 circuits, main circuit main
module main (
  input  S0,
  input  S1,
  input  [2:0] D0,
  input  [2:0] D1,
  input  [2:0] D2,
  input  [2:0] D3,
  output [2:0] Y
);

  wire and_1_out, and_2_out, and_3_out, and_4_out, and_5_out, and_6_out, and_7_out, and_8_out, and_9_out,
       and_10_out, and_11_out, and_12_out, decoder2to4_1_out_3, decoder2to4_1_out_4, decoder2to4_1_out_5,
       decoder2to4_1_out_6;

  decoder2to4 decoder2to4_1 (
    .in_1(S1), .in_2(S0), .out_3(decoder2to4_1_out_3), .out_4(decoder2to4_1_out_4),
    .out_5(decoder2to4_1_out_5), .out_6(decoder2to4_1_out_6));
  and and_1 (and_1_out, decoder2to4_1_out_3, D0[0]);
  and and_2 (and_2_out, D0[1], decoder2to4_1_out_3);
  and and_3 (and_3_out, D0[2], decoder2to4_1_out_3);
  and and_4 (and_4_out, D1[0], decoder2to4_1_out_4);
  and and_5 (and_5_out, decoder2to4_1_out_4, D1[1]);
  and and_6 (and_6_out, decoder2to4_1_out_4, D1[2]);
  and and_7 (and_7_out, D2[1], decoder2to4_1_out_5);
  and and_8 (and_8_out, D2[0], decoder2to4_1_out_5);
  and and_9 (and_9_out, D2[2], decoder2to4_1_out_5);
  and and_10 (and_10_out, decoder2to4_1_out_6, D3[0]);
  and and_11 (and_11_out, decoder2to4_1_out_6, D3[1]);
  and and_12 (and_12_out, decoder2to4_1_out_6, D3[2]);
  or or_1 (Y[0], and_1_out, and_4_out, and_7_out, and_10_out);
  or or_2 (Y[1], and_2_out, and_5_out, and_8_out, and_11_out);
  or or_3 (Y[2], and_3_out, and_6_out, and_9_out, and_12_out);
endmodule

module decoder2to4 (
  input  in_1,
  input  in_2,
  output out_3,
  output out_4,
  output out_5,
  output out_6
);

  wire not_1_out, not_2_out;

  not not_1 (not_1_out, in_1);
  not not_2 (not_2_out, in_2);
  and and_1 (out_3, not_1_out, not_2_out);
  and and_2 (out_4, in_1, not_2_out);
  and and_3 (out_5, in_1, not_2_out);
  and and_4 (out_6, in_1, in_2);
endmodule
