// Logisim project 1 7_Seg_Disp_2.circ as structural Verilog: 3 circuits, main circuit main
module main (
  input  in_1
);

  wire A_out, B_out, C_out, D_out, decoder4_16_1_out_6, decoder4_16_1_out_7, decoder4_16_1_out_8,
       decoder4_16_1_out_9, decoder4_16_1_out_10, decoder4_16_1_out_11, decoder4_16_1_out_12,
       decoder4_16_1_out_13, decoder4_16_1_out_14, decoder4_16_1_out_15, decoder4_16_1_out_16,
       decoder4_16_1_out_17, decoder4_16_1_out_18, decoder4_16_1_out_19, decoder4_16_1_out_20,
       decoder4_16_1_out_21, dipswitch_1_p1, dipswitch_1_p2, dipswitch_1_p3, dipswitch_1_p4, E_out, F_out,
       G_out;

  // DipSwitch #(.number(4)) dipswitch_1: pin names not known; wires that end beside it: dipswitch_1_p1, dipswitch_1_p2, dipswitch_1_p3, dipswitch_1_p4
  decoder4_16 decoder4_16_1 (
    .EN(in_1), .in_2(dipswitch_1_p1), .in_3(dipswitch_1_p2), .in_4(dipswitch_1_p3), .in_5(dipswitch_1_p4),
    .out_6(decoder4_16_1_out_6), .out_7(decoder4_16_1_out_7), .out_8(decoder4_16_1_out_8),
    .out_9(decoder4_16_1_out_9), .out_10(decoder4_16_1_out_10), .out_11(decoder4_16_1_out_11),
    .out_12(decoder4_16_1_out_12), .out_13(decoder4_16_1_out_13), .out_14(decoder4_16_1_out_14),
    .out_15(decoder4_16_1_out_15), .out_16(decoder4_16_1_out_16), .out_17(decoder4_16_1_out_17),
    .out_18(decoder4_16_1_out_18), .out_19(decoder4_16_1_out_19), .out_20(decoder4_16_1_out_20),
    .out_21(decoder4_16_1_out_21));
  or G (G_out, decoder4_16_1_out_13, decoder4_16_1_out_19, decoder4_16_1_out_18, decoder4_16_1_out_17, decoder4_16_1_out_16, decoder4_16_1_out_15, decoder4_16_1_out_12, decoder4_16_1_out_11, decoder4_16_1_out_10, decoder4_16_1_out_7, decoder4_16_1_out_6, decoder4_16_1_out_8);
  or F (F_out, decoder4_16_1_out_21, decoder4_16_1_out_17, decoder4_16_1_out_16, decoder4_16_1_out_15, decoder4_16_1_out_13, decoder4_16_1_out_12, decoder4_16_1_out_11, decoder4_16_1_out_10, decoder4_16_1_out_9, decoder4_16_1_out_7, decoder4_16_1_out_6);
  or A (A_out, decoder4_16_1_out_21, decoder4_16_1_out_19, decoder4_16_1_out_18, decoder4_16_1_out_16, decoder4_16_1_out_15, decoder4_16_1_out_14, decoder4_16_1_out_13, decoder4_16_1_out_12, decoder4_16_1_out_11, decoder4_16_1_out_9, decoder4_16_1_out_7, decoder4_16_1_out_6);
  or B (B_out, decoder4_16_1_out_21, decoder4_16_1_out_20, decoder4_16_1_out_19, decoder4_16_1_out_18, decoder4_16_1_out_17, decoder4_16_1_out_14, decoder4_16_1_out_13, decoder4_16_1_out_12, decoder4_16_1_out_11, decoder4_16_1_out_8);
  _7_Segment_Display u_7_segment_display_1 (
    .g(G_out), .f(F_out), .a(A_out), .b(B_out), .e(E_out), .d(D_out), .c(C_out));  // open: dp
  or C (C_out, decoder4_16_1_out_21, decoder4_16_1_out_20, decoder4_16_1_out_18, decoder4_16_1_out_17, decoder4_16_1_out_16, decoder4_16_1_out_15, decoder4_16_1_out_14, decoder4_16_1_out_13, decoder4_16_1_out_12, decoder4_16_1_out_11, decoder4_16_1_out_10, decoder4_16_1_out_8);
  or D (D_out, decoder4_16_1_out_21, decoder4_16_1_out_19, decoder4_16_1_out_18, decoder4_16_1_out_16, decoder4_16_1_out_15, decoder4_16_1_out_13, decoder4_16_1_out_12, decoder4_16_1_out_10, decoder4_16_1_out_9, decoder4_16_1_out_8, decoder4_16_1_out_7);
  or E (E_out, decoder4_16_1_out_21, decoder4_16_1_out_19, decoder4_16_1_out_15, decoder4_16_1_out_13, decoder4_16_1_out_11, decoder4_16_1_out_10, decoder4_16_1_out_9, decoder4_16_1_out_8, decoder4_16_1_out_7, decoder4_16_1_out_6);
endmodule

module decoder4_16 (
  input  EN,
  input  in_2,
  input  in_3,
  input  in_4,
  input  in_5,
  output out_6,
  output out_7,
  output out_8,
  output out_9,
  output out_10,
  output out_11,
  output out_12,
  output out_13,
  output out_14,
  output out_15,
  output out_16,
  output out_17,
  output out_18,
  output out_19,
  output out_20,
  output out_21
);

  wire and_1_out, and_2_out, not_1_out;

  not not_1 (not_1_out, in_2);
  and and_1 (and_1_out, EN, in_2);
  and and_2 (and_2_out, EN, not_1_out);
  decoder3_8 decoder3_8_1 (
    .EN(and_1_out), .A2(in_3), .A1(in_4), .A0(in_5), .out_5(out_6), .out_6(out_7), .out_7(out_8),
    .out_8(out_9), .out_9(out_10), .out_10(out_11), .out_11(out_12), .out_12(out_13));
  decoder3_8 decoder3_8_2 (
    .EN(and_2_out), .A2(in_3), .A1(in_4), .A0(in_5), .out_5(out_14), .out_6(out_15), .out_7(out_16),
    .out_8(out_17), .out_9(out_18), .out_10(out_19), .out_11(out_20), .out_12(out_21));
endmodule

module decoder3_8 (
  input  EN,
  input  A2,
  input  A1,
  input  A0,
  output out_5,
  output out_6,
  output out_7,
  output out_8,
  output out_9,
  output out_10,
  output out_11,
  output out_12
);

  wire not_1_out, not_2_out, not_3_out;

  not not_1 (not_1_out, A2);
  not not_2 (not_2_out, A1);
  not not_3 (not_3_out, A0);
  and and_1 (out_5, A2, A1, A0, EN);
  and and_2 (out_6, A2, A1, not_3_out, EN);
  and and_3 (out_7, A2, not_2_out, A0, EN);
  and and_4 (out_8, A2, not_2_out, not_3_out, EN);
  and and_5 (out_9, not_1_out, A1, A0, EN);
  and and_6 (out_10, not_1_out, A1, not_3_out, EN);
  and and_7 (out_11, not_1_out, not_2_out, A0, EN);
  and and_8 (out_12, not_1_out, not_2_out, not_3_out, EN);
endmodule
