// Logisim project 2.7_Seg_Disp.circ as structural Verilog: 3 circuits, main circuit main
module main (
);

  wire A_out, and_1_out, and_2_out, and_3_out, and_4_out, and_5_out, and_6_out, and_7_out, and_8_out, B_out,
       C_out, D_out, dipswitch_1_p1, dipswitch_1_p2, dipswitch_1_p3, dipswitch_1_p4, dipswitch_1_p5,
       dipswitch_1_p6, dipswitch_1_p7, dipswitch_1_p8, dipswitch_1_p9, dipswitch_2_p1, dipswitch_2_p2,
       dipswitch_2_p3, dipswitch_2_p4, dipswitch_2_p5, dipswitch_2_p6, dipswitch_2_p7, dipswitch_2_p8, E_out,
       encoder4_2_1_y0, encoder4_2_1_y1, encoder4_2_2_y0, encoder4_2_2_y1, encoder4_2_3_y0, encoder4_2_3_y1,
       encoder4_2_4_y0, encoder4_2_4_y1, encoder4_16_1_f0, encoder4_16_1_f1, encoder4_16_1_f2,
       encoder4_16_1_f3, encoder4_16_1_f4, encoder4_16_1_f5, encoder4_16_1_f6, encoder4_16_1_f7,
       encoder4_16_1_f8, encoder4_16_1_f9, encoder4_16_1_f10, encoder4_16_1_f11, encoder4_16_1_f12,
       encoder4_16_1_f13, encoder4_16_1_f14, encoder4_16_1_f15, F_out, G_out, or_1_out, or_2_out, or_3_out,
       or_4_out, V0_out, V2_out, V3_out;

  // DipSwitch dipswitch_1: pin names not known; wires that end beside it: dipswitch_1_p1, dipswitch_1_p2, dipswitch_1_p3, dipswitch_1_p4, dipswitch_1_p5, dipswitch_1_p6, dipswitch_1_p7, dipswitch_1_p8, dipswitch_1_p9
  // DipSwitch dipswitch_2: pin names not known; wires that end beside it: dipswitch_2_p1, dipswitch_2_p2, dipswitch_2_p3, dipswitch_2_p4, dipswitch_2_p5, dipswitch_2_p6, dipswitch_2_p7, dipswitch_2_p8
  or V0 (V0_out, dipswitch_1_p1, dipswitch_1_p2, dipswitch_1_p3, dipswitch_1_p4);
  or V1 (dipswitch_1_p9, dipswitch_1_p5, dipswitch_1_p6, dipswitch_1_p7, dipswitch_1_p8);
  or V2 (V2_out, dipswitch_2_p4, dipswitch_2_p3, dipswitch_2_p2, dipswitch_2_p1);
  or V3 (V3_out, dipswitch_2_p8, dipswitch_2_p7, dipswitch_2_p6, dipswitch_2_p5);
  encoder4_2 encoder4_2_1 (
    .EN(V0_out), .A0(dipswitch_1_p1), .A1(dipswitch_1_p2), .A2(dipswitch_1_p3), .A3(dipswitch_1_p4),
    .Y0(encoder4_2_1_y0), .Y1(encoder4_2_1_y1));
  encoder4_2 encoder4_2_2 (
    .EN(dipswitch_1_p9), .A0(dipswitch_1_p5), .A1(dipswitch_1_p6), .A2(dipswitch_1_p7), .A3(dipswitch_1_p8),
    .Y0(encoder4_2_2_y0), .Y1(encoder4_2_2_y1));
  encoder4_2 encoder4_2_3 (
    .EN(V2_out), .A0(dipswitch_2_p1), .A1(dipswitch_2_p2), .A2(dipswitch_2_p3), .A3(dipswitch_2_p4),
    .Y0(encoder4_2_3_y0), .Y1(encoder4_2_3_y1));
  encoder4_2 encoder4_2_4 (
    .EN(V3_out), .A0(dipswitch_2_p5), .A1(dipswitch_2_p6), .A2(dipswitch_2_p7), .A3(dipswitch_2_p8),
    .Y0(encoder4_2_4_y0), .Y1(encoder4_2_4_y1));
  and and_1 (and_1_out, encoder4_2_1_y0, V0_out);
  and and_2 (and_2_out, V0_out, encoder4_2_1_y1);
  and and_3 (and_3_out, encoder4_2_2_y0, dipswitch_1_p9);
  and and_4 (and_4_out, dipswitch_1_p9, encoder4_2_2_y1);
  and and_5 (and_5_out, encoder4_2_3_y0, V2_out);
  and and_6 (and_6_out, V2_out, encoder4_2_3_y1);
  and and_7 (and_7_out, encoder4_2_4_y0, V3_out);
  and and_8 (and_8_out, V3_out, encoder4_2_4_y1);
  or or_1 (or_1_out, and_1_out, and_3_out, and_5_out, and_7_out);
  or or_2 (or_2_out, and_2_out, and_4_out, and_6_out, and_8_out);
  or or_3 (or_3_out, dipswitch_1_p9, V3_out);
  or or_4 (or_4_out, V2_out, V3_out);
  Encoder4_16 encoder4_16_1 (
    .E0(or_1_out), .E1(or_2_out), .E2(or_3_out), .E3(or_4_out), .F0(encoder4_16_1_f0), .F1(encoder4_16_1_f1),
    .F2(encoder4_16_1_f2), .F3(encoder4_16_1_f3), .F4(encoder4_16_1_f4), .F5(encoder4_16_1_f5),
    .F6(encoder4_16_1_f6), .F7(encoder4_16_1_f7), .F8(encoder4_16_1_f8), .F9(encoder4_16_1_f9),
    .F10(encoder4_16_1_f10), .F11(encoder4_16_1_f11), .F12(encoder4_16_1_f12), .F13(encoder4_16_1_f13),
    .F14(encoder4_16_1_f14), .F15(encoder4_16_1_f15));
  or G (G_out, encoder4_16_1_f15, encoder4_16_1_f14, encoder4_16_1_f13, encoder4_16_1_f11, encoder4_16_1_f10, encoder4_16_1_f9, encoder4_16_1_f8, encoder4_16_1_f2, encoder4_16_1_f3, encoder4_16_1_f4, encoder4_16_1_f6, encoder4_16_1_f5);
  or F (F_out, encoder4_16_1_f15, encoder4_16_1_f14, encoder4_16_1_f12, encoder4_16_1_f11, encoder4_16_1_f10, encoder4_16_1_f9, encoder4_16_1_f8, encoder4_16_1_f0, encoder4_16_1_f4, encoder4_16_1_f6, encoder4_16_1_f5);
  or A (A_out, encoder4_16_1_f15, encoder4_16_1_f14, encoder4_16_1_f12, encoder4_16_1_f10, encoder4_16_1_f9, encoder4_16_1_f8, encoder4_16_1_f0, encoder4_16_1_f2, encoder4_16_1_f3, encoder4_16_1_f6, encoder4_16_1_f5, encoder4_16_1_f7);
  or B (B_out, encoder4_16_1_f13, encoder4_16_1_f10, encoder4_16_1_f9, encoder4_16_1_f8, encoder4_16_1_f0, encoder4_16_1_f1, encoder4_16_1_f2, encoder4_16_1_f3, encoder4_16_1_f6, encoder4_16_1_f7);
  _7_Segment_Display u_7_segment_display_1 (
    .g(G_out), .f(F_out), .a(A_out), .b(B_out), .e(E_out), .d(D_out), .c(C_out));  // open: dp
  or C (C_out, encoder4_16_1_f13, encoder4_16_1_f11, encoder4_16_1_f10, encoder4_16_1_f9, encoder4_16_1_f8, encoder4_16_1_f0, encoder4_16_1_f1, encoder4_16_1_f3, encoder4_16_1_f4, encoder4_16_1_f6, encoder4_16_1_f5, encoder4_16_1_f7);
  or D (D_out, encoder4_16_1_f14, encoder4_16_1_f13, encoder4_16_1_f12, encoder4_16_1_f11, encoder4_16_1_f9, encoder4_16_1_f8, encoder4_16_1_f0, encoder4_16_1_f2, encoder4_16_1_f3, encoder4_16_1_f6, encoder4_16_1_f5);
  or E (E_out, encoder4_16_1_f15, encoder4_16_1_f14, encoder4_16_1_f13, encoder4_16_1_f12, encoder4_16_1_f11, encoder4_16_1_f10, encoder4_16_1_f8, encoder4_16_1_f0, encoder4_16_1_f2, encoder4_16_1_f6);
endmodule

module encoder4_2 (
  input  EN,
  input  A0,
  input  A1,
  input  A2,
  input  A3,
  output Y0,
  output Y1
);

  wire and_1_out, and_2_out, not_1_out, not_2_out, or_1_out, or_2_out;

  not not_1 (not_1_out, A0);
  not not_2 (not_2_out, A2);
  and and_1 (and_1_out, not_1_out, A0);
  and and_2 (and_2_out, A1, not_2_out);
  or or_1 (or_1_out, and_1_out, and_2_out, A3);
  or or_2 (or_2_out, A2, A3);
  and and_3 (Y0, EN, or_1_out);
  and and_4 (Y1, or_2_out, EN);
endmodule

module Encoder4_16 (
  input  E0,
  input  E1,
  input  E2,
  input  E3,
  output F0,
  output F1,
  output F2,
  output F3,
  output F4,
  output F5,
  output F6,
  output F7,
  output F8,
  output F9,
  output F10,
  output F11,
  output F12,
  output F13,
  output F14,
  output F15
);

  wire not_1_out, not_2_out, not_3_out, not_4_out;

  not not_1 (not_1_out, E0);
  not not_2 (not_2_out, E1);
  not not_3 (not_3_out, E2);
  not not_4 (not_4_out, E3);
  and and_1 (F0, not_4_out, not_3_out, not_2_out, not_1_out);
  and and_2 (F1, E0, not_2_out, not_3_out, not_4_out);
  and and_3 (F2, E1, not_1_out, not_3_out, not_4_out);
  and and_4 (F3, E0, E1, not_3_out, not_4_out);
  and and_5 (F4, not_1_out, not_2_out, E2, not_4_out);
  and and_6 (F5, E0, E2, not_2_out, not_4_out);
  and and_7 (F6, E1, E2, not_1_out, not_4_out);
  and and_8 (F7, E0, E1, E2, not_4_out);
  and and_9 (F8, E3, not_3_out, not_2_out, not_1_out);
  and and_10 (F9, E3, E0, not_2_out, not_3_out);
  and and_11 (F10, E3, E1, not_1_out, not_3_out);
  and and_12 (F11, E3, E0, E1, not_3_out);
  and and_13 (F12, E2, E3, not_2_out, not_1_out);
  and and_14 (F13, E2, E0, E3, not_2_out);
  and and_15 (F14, E1, not_1_out, E2, E3);
  and and_16 (F15, E0, E1, E3, E2);
endmodule
