// Logisim project 24_38_end.circ as structural Verilog: 2 circuits, main circuit main
module main (
  input  EN,
  input  A1,
  input  A0,
  output Y7,
  output Y6,
  output Y5,
  output Y4,
  output Y3,
  output Y2,
  output Y1,
  output Y0
);

  wire not_1_out;

  not not_1 (not_1_out, EN);
  TO24 to24_1 (.EN(EN), .A1(A1), .A0(A0), .Y3(Y7), .Y2(Y6), .Y1(Y5), .Y0(Y4));
  TO24 to24_2 (.EN(not_1_out), .A1(A1), .A0(A0), .Y3(Y3), .Y2(Y2), .Y1(Y1), .Y0(Y0));
endmodule

module TO24 (
  input  EN,
  input  A1,
  input  A0,
  output Y3,
  output Y2,
  output Y1,
  output Y0
);

  wire not_1_out, not_2_out;

  not not_1 (not_1_out, A1);
  not not_2 (not_2_out, A0);
  and and_1 (Y3, A1, EN, A0);
  and and_2 (Y2, A1, EN, not_2_out);
  and and_3 (Y1, not_1_out, EN, A0);
  and and_4 (Y0, not_1_out, EN, not_2_out);
endmodule
