// Logisim project 3 7_Seg_Disp.circ as structural Verilog: 3 circuits, main circuit main
module main (
  input  EN
);

  wire A_out, and_1_out, and_2_out, and_3_out, and_4_out, and_5_out, and_6_out, and_7_out, B_out, C_out,
       D_out, decoder4_16_1_y0, decoder4_16_1_y1, decoder4_16_1_y2, decoder4_16_1_y3, decoder4_16_1_y4,
       decoder4_16_1_y5, decoder4_16_1_y6, decoder4_16_1_y7, decoder4_16_1_y8, decoder4_16_1_y9,
       decoder4_16_1_y10, decoder4_16_1_y11, decoder4_16_1_y12, decoder4_16_1_y13, decoder4_16_1_y14,
       decoder4_16_1_y15, decoder4_16_2_y10, decoder4_16_2_y11, decoder4_16_2_y12, decoder4_16_2_y13,
       decoder4_16_2_y14, decoder4_16_2_y15, dipswitch_1_p1, dipswitch_1_p2, dipswitch_1_p3, dipswitch_1_p4,
       dipswitch_1_p5, E_out, F_out, G_out, not_1_out, or_1_out;

  // DipSwitch #(.number(5)) dipswitch_1: pin names not known; wires that end beside it: dipswitch_1_p1, dipswitch_1_p2, dipswitch_1_p3, dipswitch_1_p4, dipswitch_1_p5
  not not_1 (not_1_out, dipswitch_1_p5);
  or or_1 (or_1_out, decoder4_16_1_y10, decoder4_16_1_y11, decoder4_16_1_y12, decoder4_16_1_y13, decoder4_16_1_y14, decoder4_16_1_y15);
  decoder4_16 decoder4_16_1 (
    .EN(EN), .in_2(dipswitch_1_p4), .in_3(dipswitch_1_p3), .in_4(dipswitch_1_p2), .in_5(dipswitch_1_p1),
    .Y15(decoder4_16_1_y15), .Y14(decoder4_16_1_y14), .Y13(decoder4_16_1_y13), .Y12(decoder4_16_1_y12),
    .Y11(decoder4_16_1_y11), .Y10(decoder4_16_1_y10), .Y9(decoder4_16_1_y9), .Y8(decoder4_16_1_y8),
    .Y7(decoder4_16_1_y7), .Y6(decoder4_16_1_y6), .Y5(decoder4_16_1_y5), .Y4(decoder4_16_1_y4),
    .Y3(decoder4_16_1_y3), .Y2(decoder4_16_1_y2), .Y1(decoder4_16_1_y1), .Y0(decoder4_16_1_y0));
  and and_1 (and_1_out, or_1_out, not_1_out);
  and and_2 (and_2_out, dipswitch_1_p5, decoder4_16_2_y15);
  decoder4_16 decoder4_16_2 (
    .EN(EN), .in_2(dipswitch_1_p4), .in_3(dipswitch_1_p3), .in_4(dipswitch_1_p2), .in_5(dipswitch_1_p1),
    .Y15(decoder4_16_2_y15), .Y14(decoder4_16_2_y14), .Y13(decoder4_16_2_y13), .Y12(decoder4_16_2_y12),
    .Y11(decoder4_16_2_y11), .Y10(decoder4_16_2_y10));  // open: Y9, Y8, Y7, Y6, Y5, Y4, Y3, Y2, Y1, Y0
  and and_3 (and_3_out, dipswitch_1_p5, decoder4_16_2_y14);
  and and_4 (and_4_out, dipswitch_1_p5, decoder4_16_2_y13);
  and and_5 (and_5_out, dipswitch_1_p5, decoder4_16_2_y12);
  and and_6 (and_6_out, dipswitch_1_p5, decoder4_16_2_y10);
  and and_7 (and_7_out, dipswitch_1_p5, decoder4_16_2_y11);
  or B (B_out, and_4_out, and_6_out, decoder4_16_1_y9, decoder4_16_1_y8, decoder4_16_1_y7, decoder4_16_1_y4, decoder4_16_1_y3, decoder4_16_1_y2, decoder4_16_1_y1, decoder4_16_1_y0);
  or A (A_out, and_2_out, and_3_out, and_5_out, and_6_out, decoder4_16_1_y9, decoder4_16_1_y8, decoder4_16_1_y7, decoder4_16_1_y6, decoder4_16_1_y5, decoder4_16_1_y3, decoder4_16_1_y2, decoder4_16_1_y0);
  or F (F_out, and_2_out, and_3_out, and_5_out, and_7_out, and_6_out, decoder4_16_1_y9, decoder4_16_1_y8, decoder4_16_1_y6, decoder4_16_1_y5, decoder4_16_1_y4, decoder4_16_1_y0);
  or G (G_out, and_2_out, and_3_out, and_4_out, and_7_out, and_6_out, decoder4_16_1_y9, decoder4_16_1_y8, decoder4_16_1_y6, decoder4_16_1_y5, decoder4_16_1_y4, decoder4_16_1_y3, decoder4_16_1_y2);
  or E (E_out, and_2_out, and_3_out, and_4_out, and_5_out, and_7_out, and_6_out, decoder4_16_1_y8, decoder4_16_1_y6, decoder4_16_1_y2, decoder4_16_1_y0);
  or D (D_out, and_4_out, and_5_out, and_7_out, and_3_out, decoder4_16_1_y9, decoder4_16_1_y8, decoder4_16_1_y6, decoder4_16_1_y5, decoder4_16_1_y3, decoder4_16_1_y2, decoder4_16_1_y0);
  or C (C_out, and_4_out, and_7_out, and_6_out, decoder4_16_1_y9, decoder4_16_1_y8, decoder4_16_1_y7, decoder4_16_1_y6, decoder4_16_1_y5, decoder4_16_1_y4, decoder4_16_1_y3, decoder4_16_1_y1, decoder4_16_1_y0);
  _7_Segment_Display u_7_segment_display_1 (
    .g(G_out), .f(F_out), .a(A_out), .b(B_out), .e(E_out), .d(D_out), .c(C_out), .dp(and_1_out));

  // Notes on the sheet:
  //   5 select  
endmodule

module decoder4_16 (
  input  EN,
  input  in_2,
  input  in_3,
  input  in_4,
  input  in_5,
  output Y15,
  output Y14,
  output Y13,
  output Y12,
  output Y11,
  output Y10,
  output Y9,
  output Y8,
  output Y7,
  output Y6,
  output Y5,
  output Y4,
  output Y3,
  output Y2,
  output Y1,
  output Y0
);

  wire and_1_out, and_2_out, not_1_out;

  not not_1 (not_1_out, in_2);
  and and_1 (and_1_out, EN, in_2);
  and and_2 (and_2_out, EN, not_1_out);
  decoder3_8 decoder3_8_1 (
    .EN(and_1_out), .A2(in_3), .A1(in_4), .A0(in_5), .out_5(Y15), .out_6(Y14), .out_7(Y13), .out_8(Y12),
    .out_9(Y11), .out_10(Y10), .out_11(Y9), .out_12(Y8));
  decoder3_8 decoder3_8_2 (
    .EN(and_2_out), .A2(in_3), .A1(in_4), .A0(in_5), .out_5(Y7), .out_6(Y6), .out_7(Y5), .out_8(Y4),
    .out_9(Y3), .out_10(Y2), .out_11(Y1), .out_12(Y0));
endmodule

module decoder3_8 (
  input  EN,
  input  A2,
  input  A1,
  input  A0,
  output out_5,
  output out_6,
  output out_7,
  output out_8,
  output out_9,
  output out_10,
  output out_11,
  output out_12
);

  wire not_1_out, not_2_out, not_3_out;

  not not_1 (not_1_out, A2);
  not not_2 (not_2_out, A1);
  not not_3 (not_3_out, A0);
  and and_1 (out_5, A2, A1, A0, EN);
  and and_2 (out_6, A2, A1, not_3_out, EN);
  and and_3 (out_7, A2, not_2_out, A0, EN);
  and and_4 (out_8, A2, not_2_out, not_3_out, EN);
  and and_5 (out_9, not_1_out, A1, A0, EN);
  and and_6 (out_10, not_1_out, A1, not_3_out, EN);
  and and_7 (out_11, not_1_out, not_2_out, A0, EN);
  and and_8 (out_12, not_1_out, not_2_out, not_3_out, EN);
endmodule
