// Logisim project 3.4to2mux.circ as structural Verilog: 1 circuit, main circuit main
module main (
  input  [2:0] D0,
  input  [2:0] D1,
  input  [2:0] S0,
  input  [2:0] S1,
  input  [2:0] D2,
  input  [2:0] D3,
  output [2:0] out_7,
  output [2:0] out_8,
  output [2:0] out_9,
  output [2:0] out_10
);

  wire [2:0] not_1_out, not_2_out;

  assign not_1_out = ~S0;  // NOT_Gate not_1, 3 bits wide
  assign not_2_out = ~S1;  // NOT_Gate not_2, 3 bits wide
  assign out_7 = D0 & not_1_out & not_2_out;  // AND_Gate and_1, 3 bits wide
  assign out_8 = D1 & not_2_out & S0;  // AND_Gate and_2, 3 bits wide
  assign out_9 = not_1_out & S1 & D2;  // AND_Gate and_3, 3 bits wide
  assign out_10 = S0 & S1 & D3;  // AND_Gate and_4, 3 bits wide
endmodule
