// Logisim project 3_to_8.circ as structural Verilog: 1 circuit, main circuit main
module main (
  input  C,
  input  B,
  input  A,
  output Y0,
  output Y1,
  output Y2,
  output Y3,
  output Y4,
  output Y5,
  output Y6,
  output Y7
);

  wire not_1_out, not_2_out, not_3_out;

  not not_1 (not_1_out, A);
  not not_2 (not_2_out, B);
  not not_3 (not_3_out, C);
  and and_1 (Y0, not_1_out, not_2_out, not_3_out);
  and and_2 (Y1, A, not_2_out, not_3_out);
  and and_3 (Y2, not_1_out, B, not_3_out);
  and and_4 (Y3, A, B, not_3_out);
  and and_5 (Y4, not_1_out, not_2_out, C);
  and and_6 (Y5, A, not_2_out, C);
  and and_7 (Y6, not_1_out, B, C);
  and and_8 (Y7, A, B, C);
endmodule
