// Logisim project 5_1.circ as structural Verilog: 1 circuit, main circuit main
module main (
  input  in_1,
  input  in_2,
  input  in_3,
  output C,
  output S
);

  wire and_1_out, and_2_out, and_3_out, xor_1_out;

  and and_1 (and_1_out, in_1, in_2);
  and and_2 (and_2_out, in_1, in_3);
  and and_3 (and_3_out, in_2, in_3);
  xor xor_1 (xor_1_out, in_1, in_3);
  or or_1 (C, and_1_out, and_2_out, and_3_out);
  xor xor_2 (S, xor_1_out, in_2);
endmodule
