// Logisim project Subcircuits.circ as structural Verilog: 2 circuits, main circuit main
module main (
  input  in_1,
  input  in_2,
  input  in_3,
  input  in_4,
  output out_5,
  output out_6,
  output out_7,
  output out_8,
  output out_9,
  output out_10,
  output out_11,
  output out_12,
  output out_13,
  output out_14
);

  wire hc139_1_out_4, hc139_1_out_5, hc139_1_out_6, hc139_1_out_7, hc139_1_out_8, hc139_1_out_9,
       hc139_1_out_10, hc139_1_out_11, not_1_out;

  HC139 hc139_1 (
    .in_1(in_2), .in_2(in_3), .in_3(in_4), .out_4(hc139_1_out_4), .out_5(hc139_1_out_5),
    .out_6(hc139_1_out_6), .out_7(hc139_1_out_7), .out_8(hc139_1_out_8), .out_9(hc139_1_out_9),
    .out_10(hc139_1_out_10), .out_11(hc139_1_out_11));
  not not_1 (not_1_out, in_1);
  and and_1 (out_13, hc139_1_out_4, in_1);
  and and_2 (out_14, hc139_1_out_5, in_1);
  and and_3 (out_5, hc139_1_out_4, not_1_out);
  and and_4 (out_6, hc139_1_out_5, not_1_out);
  and and_5 (out_7, hc139_1_out_6, not_1_out);
  and and_6 (out_8, hc139_1_out_7, not_1_out);
  and and_7 (out_9, hc139_1_out_8, not_1_out);
  and and_8 (out_10, hc139_1_out_9, not_1_out);
  and and_9 (out_11, hc139_1_out_10, not_1_out);
  and and_10 (out_12, hc139_1_out_11, not_1_out);
endmodule

module HC139 (
  input  in_1,
  input  in_2,
  input  in_3,
  output out_4,
  output out_5,
  output out_6,
  output out_7,
  output out_8,
  output out_9,
  output out_10,
  output out_11
);

  wire not_1_out, not_2_out, not_3_out;

  not not_1 (not_1_out, in_1);
  not not_2 (not_2_out, in_2);
  not not_3 (not_3_out, in_3);
  and and_1 (out_4, not_1_out, not_2_out, not_3_out);
  and and_2 (out_5, not_1_out, not_2_out, in_3);
  and and_3 (out_6, not_1_out, in_2, not_3_out);
  and and_4 (out_7, not_1_out, in_2, in_3);
  and and_5 (out_8, in_1, not_2_out, not_3_out);
  and and_6 (out_9, in_1, not_2_out, in_3);
  and and_7 (out_10, in_1, in_2, not_2_out);
  and and_8 (out_11, in_1, in_2, in_3);
endmodule
