// Logisim project 511.circ as structural Verilog: 2 circuits, main circuit main
module main (
  input  A,
  input  B,
  input  C0,
  output out_4,
  output S
);

  wire half_add_1_c0, half_add_1_s0, half_add_2_c0;

  half_add half_add_1 (.A(A), .B(B), .C0(half_add_1_c0), .S0(half_add_1_s0));
  half_add half_add_2 (.A(half_add_1_s0), .B(C0), .C0(half_add_2_c0), .S0(S));
  or or_1 (out_4, half_add_1_c0, half_add_2_c0);
endmodule

module half_add (
  input  A,
  input  B,
  output C0,
  output S0
);

  xor xor_1 (S0, A, B);
  and and_1 (C0, A, B);
endmodule
