// Logisim project NOR_1.circ as structural Verilog: 1 circuit, main circuit main
module main (
  input  A,
  input  B,
  output C
);

  wire nand_1_out, or_1_out;

  nand nand_1 (nand_1_out, A, B);
  or or_1 (or_1_out, A, B);
  and and_1 (C, nand_1_out, or_1_out);
endmodule
